// Logisim project ALU.circ as structural Verilog: 1 circuit, main circuit ALU
module ALU (
  input  [31:0] input1,
  input  [31:0] input2,
  input  [5:0] ALUOp,
  output Zero,
  output [31:0] ALUResult
);
endmodule
