// Logisim project ProgramCounter.circ as structural Verilog: 1 circuit, main circuit ProgramCounter
module ProgramCounter (
  input  [31:0] PC_in,
  output [31:0] PC_out
);

  wire CLK_out;

  Register #(.width(32)) PC (.D(PC_in), .en(1'b1), .clk(CLK_out), .Q(PC_out));  // open: clr
  Clock CLK (.out(CLK_out));
endmodule
