// Logisim project cpu.circ as structural Verilog: 2 circuits, main circuit cpu
module cpu (
  input  in_1
);

  wire ActualBranchTaken, adder_3_cout, ALU_v, ALUSrc, ALUSrc_out, ALUv_out, BEQ, BGEZ, BGTZ, BLEZ, BNE,
       Branch, BranchCheck, BranchOut, buttomLeft1RD, buttomLeft1RS, buttomLeft1RT, buttomLeftRD,
       buttomLeftRS, buttomLeftRT, buttomRD, buttomRight1RD, buttomRight1RS, buttomRight1RT, buttomRightRD,
       buttomRightRS, buttomRightRT, buttomRS, buttomRT, clk, clk_main, comparator_1_eq, Hit, JAL, Jr, Jump,
       Jump_out, LRU_OUT, LRU_TMP, MemToReg, MemToReg_out, middle1RD, middle1RS, middle1RT, middleRD,
       middleRS, middleRT, not_1_out, not_3_out, notTaken, or_4_out, or_5_out, RegDst, RegDst_out, RegWrite,
       RegWrite_out, stall, stall_done, strongly_not_taken, strongly_taken, subtractor_1_bout, syscall,
       syscall_out, taken, top1RD, top1RS, top1RT, topLeft1RD, topLeft1RS, topLeft1RT, topLeftRD, topLeftRS,
       topLeftRT, topRD, topRightRD, topRightRS, topRightRT, topRS, topRT, weakly_not_taken, weakly_taken,
       wrongPrediction;
  wire [0:0] or_3_out;
  wire [1:0] adder_3_out, inputPR, multiplexer_6_out, multiplexer_7_out, multiplexer_11_out, nextState,
       subtractor_1_out;
  wire [2:0] multiplexer_10_out, stall_num, stallOut, subtractor_2_out;
  wire [3:0] MemWriteMask, MemWriteMask_out, writeMask_cache;
  wire [4:0] multiplexer_2_out, rd, rd_out, rs, rs_out, rt, rt_out, shamt, shamt_out, writeInd;
  wire [5:0] ALU_op, ALUop_out, func, funcOut, opcode, opcode_out;
  wire [15:0] imm16, immOut;
  wire [25:0] target26, target26_out;
  wire [27:0] sxl2_1_t28;
  wire [31:0] adder_2_out, ALUResult, ALUResult_out, BResult, BResult_out, cacheOut, immIN, immINout, in1,
       in1_out, in2, in2_out, JCU_OUT, Jcu_outF, memdelayed_1_memreaddata, multiplexer_9_out, outMM, PC,
       programcounter_1_pc_out, RD1, RD1_out, RD2, RD2_out, shifter_1_out, writeback, writeback_out, writeDat;

  not not_1 (not_1_out, syscall_out);
  _7_Segment_Display u_7_segment_display_1 (
    .g(middle1RD), .f(topLeft1RD), .a(top1RD), .b(1'b1), .e(buttomLeft1RD), .d(top1RD), .c(buttomRight1RD));  // open: dp
  _7_Segment_Display u_7_segment_display_2 (
    .g(middleRD), .f(topLeftRD), .a(topRD), .b(topRightRD), .e(buttomLeftRD), .d(buttomRD), .c(buttomRightRD));  // open: dp
  display_main main_1 (
    .RegInput(rd), .buttomRight1(buttomRight1RD), .buttomRight(buttomRightRD), .buttomLeft1(buttomLeft1RD),
    .buttomLeft(buttomLeftRD), .buttom(buttomRD), .middle(middleRD), .middle1(middle1RD), .top(topRD),
    .top1(top1RD), .topLeft(topLeftRD), .topLeft1(topLeft1RD), .topRight(topRightRD));
  display_main main_2 (
    .RegInput(rs), .buttomRight1(buttomRight1RS), .buttomRight(buttomRightRS), .buttomLeft1(buttomLeft1RS),
    .buttomLeft(buttomLeftRS), .buttom(buttomRS), .middle(middleRS), .middle1(middle1RS), .top(topRS),
    .top1(top1RS), .topLeft(topLeftRS), .topLeft1(topLeft1RS), .topRight(topRightRS));
  display_main main_3 (
    .RegInput(rt), .buttomRight1(buttomRight1RT), .buttomRight(buttomRightRT), .buttomLeft1(buttomLeft1RT),
    .buttomLeft(buttomLeftRT), .buttom(buttomRT), .middle(middleRT), .middle1(middle1RT), .top(topRT),
    .top1(top1RT), .topLeft(topLeftRT), .topLeft1(topLeft1RT), .topRight(topRightRT));
  Adder #(.width(32)) adder_1 (.a(programcounter_1_pc_out), .b(32'h4), .out(in2));  // open: cin, cout
  ProgramCounter programcounter_1 (.PC_in(PC), .En(not_1_out), .CLK(clk), .PC_out(programcounter_1_pc_out));
  Multiplexer #(.width(32)) multiplexer_1 (
    .in0(BResult_out), .in1({in2[31:28], sxl2_1_t28}), .out(in1), .sel(Jump_out));
  _7_Segment_Display u_7_segment_display_3 (
    .g(middle1RS), .f(topLeft1RS), .a(top1RS), .b(1'b1), .e(buttomLeft1RS), .d(top1RS), .c(buttomRight1RS));  // open: dp
  _7_Segment_Display u_7_segment_display_4 (
    .g(middleRS), .f(topLeftRS), .a(topRS), .b(topRightRS), .e(buttomLeftRS), .d(buttomRS), .c(buttomRightRS));  // open: dp
  SXL2 sxl2_1 (.T26(target26), .T28(sxl2_1_t28));
  memDelayed memdelayed_1 (
    .MemAddress(programcounter_1_pc_out), .clk(clk), .MemReadData(memdelayed_1_memreaddata));  // open: MemWriteMask, MemWriteData
  _7_Segment_Display u_7_segment_display_5 (
    .g(middle1RT), .f(topLeft1RT), .a(top1RT), .b(1'b1), .e(buttomLeft1RT), .d(top1RT), .c(buttomRight1RT));  // open: dp
  instruction_splitter instruction_splitter_1 (
    .instruction(memdelayed_1_memreaddata), .op(opcode), .target26(target26), .rs(rs), .rt(rt),
    .imm16(imm16), .rd(rd), .shamt(shamt), .func(func));
  _7_Segment_Display u_7_segment_display_6 (
    .g(middleRT), .f(topLeftRT), .a(topRT), .b(topRightRT), .e(buttomLeftRT), .d(buttomRT), .c(buttomRightRT));  // open: dp
  Register #(.width(32)) register_1 (.D(in2), .en(1'b1), .clk(clk), .Q(in2_out), .clr(in_1));
  Register #(.width(32)) register_2 (.D(in1), .en(1'b1), .clk(clk), .Q(in1_out), .clr(in_1));
  Register #(.width(6)) register_3 (.D(opcode), .en(1'b1), .clk(clk), .Q(opcode_out), .clr(in_1));
  Register #(.width(26)) register_4 (.D(target26), .en(1'b1), .clk(clk), .Q(target26_out), .clr(in_1));
  Register #(.width(5)) register_5 (.D(rs), .en(1'b1), .clk(clk), .Q(rs_out), .clr(in_1));
  Register #(.width(5)) register_6 (.D(rt), .en(1'b1), .clk(clk), .Q(rt_out), .clr(in_1));
  Register #(.width(16)) register_7 (.D(imm16), .en(1'b1), .clk(clk), .Q(immOut), .clr(in_1));
  Register #(.width(5)) register_8 (.D(rd), .en(1'b1), .Q(rd_out), .clr(in_1));  // open: clk
  Register #(.width(5)) register_9 (.D(shamt), .en(1'b1), .clk(clk), .Q(shamt_out), .clr(in_1));
  Register #(.width(6)) register_10 (.D(func), .en(1'b1), .clk(clk), .Q(funcOut), .clr(in_1));
  Multiplexer #(.width(5)) multiplexer_2 (.in0(rt_out), .in1(rd_out), .out(multiplexer_2_out), .sel(RegDst));
  Multiplexer #(.width(32)) multiplexer_3 (.in0(writeback_out), .in1(JCU_OUT), .out(writeDat), .sel(JAL));
  Multiplexer #(.width(5)) multiplexer_4 (.in0(multiplexer_2_out), .in1({5{1'b1}}), .out(writeInd), .sel(JAL));
  JCU jcu_1 (.Func(funcOut), .in1(in1_out), .rs(rs_out), .Y(JCU_OUT));
  // CU cu_1: pin names not known; wires that end beside it: funcOut, opcode_out, JAL, ALUSrc, ALU_op, syscall, RegDst, ALU_v, MemToReg, RegWrite, MemWriteMask, Branch, Jump, Jr
  SignExtend signextend_1 (.S16(immOut), .S32(immIN));
  regfile regfile_1 (
    .ReadIndex1(rs_out), .ReadIndex2(rt_out), .WriteIndex(writeInd), .WriteData(writeDat), .RegWEn(RegWrite),
    .clk(clk), .ReadData1(RD1), .ReadData2(RD2));
  Register #(.width(32)) register_11 (.D(immIN), .en(1'b1), .clk(clk), .Q(immINout), .clr(in_1));
  Register #(.width(32)) register_12 (.D(JCU_OUT), .en(1'b1), .clk(clk), .Q(Jcu_outF), .clr(in_1));
  Register #(.width(1)) register_13 (.D(ALUSrc), .en(1'b1), .clk(clk), .Q(ALUSrc_out), .clr(in_1));
  Register #(.width(6)) register_14 (.D(ALU_op), .en(1'b1), .clk(clk), .Q(ALUop_out), .clr(in_1));
  Register #(.width(1)) register_15 (.D(RegDst), .en(1'b1), .clk(clk), .Q(RegDst_out), .clr(in_1));
  Register #(.width(1)) register_16 (.D(ALU_v), .en(1'b1), .clk(clk), .Q(ALUv_out), .clr(in_1));
  Register #(.width(1)) register_17 (.D(MemToReg), .en(1'b1), .clk(clk), .Q(MemToReg_out), .clr(in_1));
  Register #(.width(1)) register_18 (.D(RegWrite), .en(1'b1), .clk(clk), .Q(RegWrite_out), .clr(in_1));
  Register #(.width(4)) register_19 (.D(MemWriteMask), .en(1'b1), .clk(clk), .Q(MemWriteMask_out), .clr(in_1));
  Register #(.width(1)) register_20 (.D(Branch), .en(1'b1), .clk(clk), .Q(BranchOut), .clr(in_1));
  Register #(.width(1)) register_21 (.D(Jump), .en(1'b1), .clk(clk), .Q(Jump_out), .clr(in_1));
  Register #(.width(32)) register_22 (.D(RD1), .en(1'b1), .clk(clk), .Q(RD1_out), .clr(in_1));
  Register #(.width(32)) register_23 (.D(RD2), .en(1'b1), .clk(clk), .Q(RD2_out), .clr(in_1));
  Register #(.width(1)) register_24 (.D(syscall), .en(1'b1), .clk(clk), .Q(syscall_out), .clr(in_1));
  Shifter #(.width(32)) shifter_1 (.in(immINout), .\dist (5'b00010), .out(shifter_1_out));
  Decoder #(.select(3)) decoder_1 (
    .out1(BGEZ), .out4(BEQ), .out5(BNE), .out6(BLEZ), .out7(BGTZ), .sel(opcode[5:3]), .en(Branch));  // open: out0, out2, out3
  Adder #(.width(32)) adder_2 (.a(in2_out), .b(shifter_1_out), .out(adder_2_out));  // open: cin, cout
  Multiplexer #(.width(32)) multiplexer_5 (.in0(in2_out), .in1(adder_2_out), .out(BResult), .sel(ActualBranchTaken));
  and and_1 (ActualBranchTaken, BranchOut, BranchCheck);
  ALU alu_1 (
    .A(RD1_out), .B(RD2_out), .ALUOp(ALUop_out), .Func(funcOut), .Imm(immINout), .Shamt(shamt_out),
    .ALUSrc(ALUSrc_out), .Zero(BranchCheck), .ALUResult(ALUResult));
  Register #(.width(2)) register_25 (.D(nextState), .en(BEQ), .clk(clk), .Q(inputPR), .clr(in_1));
  Register #(.width(2)) register_26 (.D(nextState), .en(BNE), .clk(clk), .Q(inputPR), .clr(in_1));
  Register #(.width(2)) register_27 (.D(nextState), .en(BLEZ), .clk(clk), .Q(inputPR), .clr(in_1));
  Register #(.width(2)) register_28 (.D(nextState), .en(BGTZ), .clk(clk), .Q(inputPR), .clr(in_1));
  Register #(.width(2)) register_29 (.D(nextState), .en(BGEZ), .clk(clk), .Q(inputPR), .clr(in_1));
  Register #(.width(32)) register_30 (.D(BResult), .en(1'b1), .clk(clk), .Q(BResult_out), .clr(in_1));
  Register #(.width(32)) register_31 (.D(ALUResult), .en(1'b1), .clk(clk), .Q(ALUResult_out), .clr(in_1));
  Decoder #(.select(2)) decoder_2 (
    .out0(strongly_not_taken), .out1(weakly_not_taken), .out2(weakly_taken), .out3(strongly_taken),
    .sel(inputPR), .en(1'b1));
  Subtractor #(.width(2)) subtractor_1 (
    .a(inputPR), .b({1'b0, notTaken}), .out(subtractor_1_out), .bout(subtractor_1_bout));  // open: bin
  Adder #(.width(2)) adder_3 (.a(inputPR), .b({1'b0, notTaken}), .out(adder_3_out), .cout(adder_3_cout));  // open: cin
  Clock clock_1 (.out(clk_main));
  or or_1 (notTaken, strongly_not_taken, weakly_not_taken);
  or or_2 (taken, weakly_taken, strongly_taken);
  Multiplexer #(.width(2)) multiplexer_6 (
    .in0(subtractor_1_out), .in1(2'b11), .out(multiplexer_6_out), .sel(subtractor_1_bout));
  Multiplexer #(.width(2)) multiplexer_7 (.in0(adder_3_out), .in1(2'b00), .out(multiplexer_7_out), .sel(adder_3_cout));
  Comparator #(.width(1)) comparator_1 (.a(taken), .b(ActualBranchTaken), .eq(comparator_1_eq));  // open: gt, lt
  Multiplexer #(.width(2)) multiplexer_8 (
    .in0(multiplexer_6_out), .in1(multiplexer_7_out), .out(nextState), .sel(ActualBranchTaken));
  not not_2 (wrongPrediction, comparator_1_eq);
  not not_3 (not_3_out, clk);
  Multiplexer #(.width(32)) multiplexer_9 (.in0(outMM), .in1(RD2_out), .out(multiplexer_9_out), .sel(Hit));
  Subtractor #(.width(3)) subtractor_2 (.a(stallOut), .b(3'b001), .out(subtractor_2_out));  // open: bin, bout
  memDelayed memdelayed_2 (
    .MemAddress(ALUResult_out), .MemWriteMask(writeMask_cache), .MemWriteData(RD2_out), .clk(not_3_out),
    .MemReadData(outMM));
  cahceCU cahcecu_1 (.CPU_Address(ALUResult_out), .LRU(LRU_OUT), .CLOCK(clk), .RESET(in_1), .LRU_out(LRU_TMP));
  cache cache_1 (
    .CPU_Address(ALUResult_out), .memWriteData(multiplexer_9_out), .MemWriteMask(MemWriteMask_out),
    .LRU(LRU_TMP), .clock(clk_main), .reset(in_1), .raedData(cacheOut), .Hit(Hit), .LRU_out(LRU_OUT),
    .writeMask(writeMask_cache));
  Comparator #(.width(3)) comparator_2 (.a(stallOut), .b(3'b000), .eq(stall_done));  // open: gt, lt
  Multiplexer #(.width(3)) multiplexer_10 (
    .in0(subtractor_2_out), .in1(stall_num), .out(multiplexer_10_out), .sel(stall));
  or or_3 (or_3_out[0], Jr, wrongPrediction);
  Register #(.width(3)) register_32 (.D(multiplexer_10_out), .en(1'b1), .clk(clk), .Q(stallOut), .clr(in_1));
  Multiplexer #(.select(2), .width(2)) multiplexer_11 (
    .in0(2'b00), .in1(2'b01), .in2(2'b10), .out(multiplexer_11_out), .sel({Branch, or_3_out[0]}));  // open: in3
  or or_4 (or_4_out, Jr, wrongPrediction);
  Multiplexer multiplexer_12 (.in0(1'b0), .in1(clk_main), .out(clk), .sel(Hit));
  Multiplexer #(.width(32)) multiplexer_13 (.in0(JCU_OUT), .in1({32{1'b1}}), .out(PC), .sel(stall));
  Register #(.width(3)) register_33 (
    .D({1'b0, multiplexer_11_out}), .en(stall), .clk(clk_main), .Q(stall_num), .clr(in_1));
  or or_5 (or_5_out, or_4_out, Branch);
  and and_2 (stall, or_5_out, stall_done);
  Multiplexer #(.width(32)) multiplexer_14 (.in0(ALUResult_out), .in1(cacheOut), .out(writeback), .sel(MemToReg_out));
  Register #(.width(32)) register_34 (.D(writeback), .en(1'b1), .clk(clk), .Q(writeback_out), .clr(in_1));

  // Other names for the same wires on the sheet: reset = in_1

  // Notes on the sheet:
  //   RD
  //   RS
  //   RT
  //   IF/ID
  //   ID/EXE
  //   100
  //   101
  //   110
  //   111
  //   001
  //   states: 00 -> strongly not taken/ 01 -> weakly not taken/ 10 -> weakly taken/ 11 -> strongly taken
  //   saturing counter value
  //   EXE/MEM
  //   PredictionLogic
  //   BRANCH PREDICTOR
  //   needs one stall
  //   needs two stalls
  //   MEM/WB
endmodule

module display (
  input  [4:0] in_1
);

  wire and_1_out, and_2_out, and_3_out, and_4_out, and_5_out, and_6_out, and_7_out, and_8_out, and_9_out,
       and_10_out, and_11_out, and_12_out, and_13_out, and_14_out, and_15_out, and_16_out, and_17_out,
       and_18_out, and_19_out, and_20_out, and_21_out, and_22_out, and_23_out, and_24_out, and_25_out,
       and_26_out, and_27_out, and_28_out, and_29_out, and_30_out, and_31_out, and_32_out, and_33_out,
       and_34_out, and_35_out, and_36_out, and_37_out, and_38_out, and_39_out, and_40_out, and_41_out,
       and_42_out, and_43_out, and_44_out, and_45_out, and_46_out, and_47_out, and_48_out, and_49_out,
       and_50_out, and_51_out, and_52_out, and_53_out, and_54_out, and_55_out, and_56_out, and_57_out,
       and_58_out, and_59_out, and_60_out, and_61_out, and_62_out, and_63_out, and_64_out, and_65_out,
       and_66_out, and_67_out, buttom, buttomLeft, buttomLeft1, buttomRight, buttomRight1, middle, middle1,
       not_1_out, not_2_out, not_3_out, not_4_out, not_5_out, not_6_out, not_7_out, not_8_out, not_9_out,
       not_11_out, not_12_out, not_13_out, not_14_out, not_15_out, not_16_out, not_17_out, not_18_out,
       not_19_out, top, top1, topLeft, topLeft1, topRight;

  _7_Segment_Display u_7_segment_display_1 (
    .g(middle1), .f(topLeft1), .a(top1), .b(1'b1), .e(buttomLeft1), .d(top1), .c(buttomRight1));  // open: dp
  _7_Segment_Display u_7_segment_display_2 (
    .g(middle), .f(topLeft), .a(top), .b(topRight), .e(buttomLeft), .d(buttom), .c(buttomRight));  // open: dp
  not not_1 (not_1_out, in_1[4]);
  not not_2 (not_2_out, in_1[3]);
  not not_3 (not_3_out, in_1[2]);
  not not_4 (not_4_out, in_1[1]);
  not not_5 (not_5_out, in_1[0]);
  and and_1 (and_1_out, not_2_out, not_4_out, not_5_out);
  not not_6 (not_6_out, in_1[4]);
  not not_7 (not_7_out, in_1[3]);
  not not_8 (not_8_out, in_1[2]);
  not not_9 (not_9_out, in_1[1]);
  // NOT_Gate not_10 has open pins: in=in_1[0], out=open
  not not_11 (not_11_out, in_1[4]);
  not not_12 (not_12_out, in_1[3]);
  not not_13 (not_13_out, in_1[2]);
  not not_14 (not_14_out, in_1[1]);
  not not_15 (not_15_out, in_1[4]);
  not not_16 (not_16_out, in_1[3]);
  not not_17 (not_17_out, in_1[2]);
  not not_18 (not_18_out, in_1[1]);
  not not_19 (not_19_out, in_1[0]);
  and and_2 (and_2_out, not_17_out, not_18_out);
  and and_3 (and_3_out, in_1[3], not_3_out, not_4_out);
  and and_4 (and_4_out, in_1[3], in_1[1], not_5_out);
  and and_5 (and_5_out, not_6_out, not_7_out);
  and and_6 (and_6_out, not_11_out, not_12_out);
  and and_7 (and_7_out, not_12_out, in_1[2]);
  or or_1 (buttomLeft1, and_6_out, and_7_out, and_15_out, and_14_out, and_20_out);
  and and_8 (and_8_out, in_1[3], in_1[1]);
  and and_9 (and_9_out, in_1[4], not_17_out);
  or or_2 (buttomRight, in_1[0], and_2_out, and_8_out, and_9_out, and_17_out, and_16_out);
  and and_10 (and_10_out, not_1_out, not_2_out, in_1[2], not_4_out);
  and and_11 (and_11_out, in_1[4], in_1[3], not_4_out);
  or or_3 (topLeft, and_1_out, and_3_out, and_4_out, and_11_out, and_10_out, and_18_out, and_21_out, and_27_out);
  and and_12 (and_12_out, in_1[4], in_1[3]);
  and and_13 (and_13_out, not_7_out, in_1[2]);
  or or_4 (top1, and_5_out, and_13_out, and_12_out, and_19_out);
  and and_14 (and_14_out, in_1[4], in_1[2], not_14_out);
  and and_15 (and_15_out, not_11_out, not_13_out, not_14_out);
  and and_16 (and_16_out, not_15_out, not_16_out, in_1[2]);
  and and_17 (and_17_out, in_1[4], not_18_out);
  and and_18 (and_18_out, not_1_out, not_2_out, in_1[2], not_5_out);
  and and_19 (and_19_out, not_6_out, not_8_out, not_9_out);
  and and_20 (and_20_out, in_1[4], in_1[3], not_13_out);
  and and_21 (and_21_out, not_1_out, in_1[3], in_1[2], in_1[1]);
  and and_22 (and_22_out, in_1[4], in_1[2]);
  and and_23 (and_23_out, in_1[4], in_1[3]);
  or or_5 (middle1, and_22_out, and_23_out);
  and and_24 (and_24_out, not_12_out, not_13_out);
  and and_25 (and_25_out, in_1[3], in_1[2], in_1[1]);
  or or_6 (buttomRight1, and_24_out, and_25_out, not_11_out);
  and and_26 (and_26_out, not_15_out, not_17_out, not_19_out);
  and and_27 (and_27_out, in_1[4], not_2_out, not_3_out, in_1[1]);
  and and_28 (and_28_out, not_6_out, not_7_out);
  and and_29 (and_29_out, not_6_out, not_8_out, not_9_out);
  or or_7 (topLeft1, and_28_out, and_29_out);
  and and_30 (and_30_out, not_16_out, not_17_out, in_1[1]);
  and and_31 (and_31_out, not_16_out, in_1[1], not_19_out);
  and and_32 (and_32_out, not_2_out, in_1[1]);
  and and_33 (and_33_out, not_1_out, not_3_out, not_5_out);
  and and_34 (and_34_out, in_1[3], not_18_out, in_1[0]);
  and and_35 (and_35_out, in_1[3], in_1[2], not_18_out);
  or or_8 (buttom, and_45_out, and_26_out, and_30_out, and_31_out, and_34_out, and_35_out, and_38_out, and_39_out, and_42_out, and_46_out);
  and and_36 (and_36_out, not_1_out, in_1[2], in_1[0]);
  and and_37 (and_37_out, not_1_out, in_1[3], not_4_out);
  or or_9 (top, and_32_out, and_33_out, and_36_out, and_37_out, and_40_out, and_41_out, and_43_out, and_44_out);
  and and_38 (and_38_out, in_1[4], not_16_out, not_19_out);
  and and_39 (and_39_out, in_1[4], not_16_out, in_1[1]);
  and and_40 (and_40_out, in_1[3], in_1[2], not_4_out);
  and and_41 (and_41_out, in_1[4], not_2_out, not_5_out);
  and and_42 (and_42_out, in_1[4], in_1[1], not_19_out);
  and and_43 (and_43_out, in_1[4], not_3_out, in_1[0]);
  and and_44 (and_44_out, in_1[4], in_1[1], not_5_out);
  and and_45 (and_45_out, not_15_out, in_1[2], not_18_out, in_1[0]);
  and and_46 (and_46_out, not_15_out, in_1[3], in_1[2], in_1[0]);
  and and_47 (and_47_out, in_1[4], in_1[2]);
  and and_48 (and_48_out, not_1_out, not_4_out, not_5_out);
  and and_49 (and_49_out, not_16_out, not_17_out, not_19_out);
  and and_50 (and_50_out, not_2_out, not_3_out, in_1[0]);
  and and_51 (and_51_out, not_2_out, not_3_out, in_1[1]);
  and and_52 (and_52_out, not_16_out, in_1[1], not_19_out);
  and and_53 (and_53_out, not_17_out, in_1[1], not_19_out);
  or or_10 (buttomLeft, and_49_out, and_52_out, and_53_out, and_56_out, and_57_out);
  and and_54 (and_54_out, not_2_out, in_1[1], in_1[0]);
  and and_55 (and_55_out, not_3_out, in_1[1], in_1[0]);
  or or_11 (topRight, and_47_out, and_48_out, and_50_out, and_51_out, and_60_out, and_54_out, and_55_out, and_58_out, and_59_out);
  and and_56 (and_56_out, in_1[4], in_1[2], not_19_out);
  and and_57 (and_57_out, not_15_out, in_1[3], not_18_out, not_19_out);
  and and_58 (and_58_out, not_1_out, in_1[3], not_4_out);
  and and_59 (and_59_out, not_1_out, in_1[3], not_5_out);
  and and_60 (and_60_out, in_1[3], not_4_out, not_5_out);
  and and_61 (and_61_out, in_1[3], not_4_out);
  and and_62 (and_62_out, not_2_out, not_3_out, in_1[1]);
  and and_63 (and_63_out, not_2_out, in_1[1], not_5_out);
  and and_64 (and_64_out, not_1_out, in_1[2], not_4_out);
  and and_65 (and_65_out, not_1_out, in_1[3], in_1[2]);
  and and_66 (and_66_out, in_1[4], not_3_out, not_5_out);
  or or_12 (middle, and_62_out, and_63_out, and_64_out, and_61_out, and_65_out, and_66_out, and_67_out);
  and and_67 (and_67_out, in_1[4], not_2_out, in_1[1]);

  // Other names for the same wires on the sheet: E = in_1[0]; D = in_1[1]; C = in_1[2]; B = in_1[3]; A = in_1[4]
endmodule
