// Logisim project set.circ as structural Verilog: 1 circuit, main circuit set
module set (
  input  [31:0] data_in,
  input  [1:0] word_index,
  input  block_index,
  input  CLOCK,
  input  RESET
);

  wire and_1_out, and_2_out, not_1_out;
  wire [31:0] code;

  and and_1 (and_1_out, CLOCK, not_1_out);
  not not_1 (not_1_out, block_index);
  and and_2 (and_2_out, CLOCK, block_index);
  B_lock block1 (.data_in(code), .word_index(word_index), .CLOCK(and_1_out), .RESET(RESET));
  B_lock block2 (.data_in(code), .word_index(word_index), .CLOCK(and_2_out), .RESET(RESET));
endmodule
